# Fritzing sketch hcsr04-5V-demo-sketch (saved by Fritzing 0.9.3b)
circuit board: 8.46667cm x 5.64444cm
breadboards: 1

parts:
  WeMos_D1_Mini1 = WeMos D1 Mini
  5VDC = Header 2 [package=molex-1x2_lock]
  hc-sr1 = hc-sr04

nets (from the schematic view):
  3V3: WeMos_D1_Mini1.3V3, hc-sr1.VCC
  N1: WeMos_D1_Mini1.5V, 5VDC.1
  N2: WeMos_D1_Mini1.D4, hc-sr1.Trig
  N3: WeMos_D1_Mini1.D6, hc-sr1.Echo
  N4: WeMos_D1_Mini1.G, 5VDC.2, hc-sr1.GND

notes:
  5V DC

custom parts:
  hc-sr04: This is a HC-SR04 Distance Sensor
