# Fritzing sketch hcsr04-demo-sketch (saved by Fritzing 0.9.3b)
breadboards: 1

parts:
  WeMos_D1_Mini1 = WeMos D1 Mini  # not connected
  hc-sr1 = hc-sr04
  JP2 = Header 2 [package=molex-1x2_lock]

nets:
  N1: hc-sr1.GND, JP2.2

notes:
  5V DC IN
